// Digital circuit additionneur_4bit.dig as structural Verilog
module additionneur_4bit (
  input  a0,
  input  b0,
  input  a1,
  input  b1,
  input  a2,
  input  b2,
  input  a3,
  input  b3,
  input  Cin,
  output S0,
  output S1,
  output S2,
  output S3
);

  wire additionneur_1bit_1_cout, additionneur_1bit_2_cout, additionneur_1bit_3_cout;

  additionneur_1bit additionneur_1bit_1 (.a(b0), .b(a0), .Cin(Cin), .S(S0), .Cout(additionneur_1bit_1_cout));
  additionneur_1bit additionneur_1bit_2 (
    .a(b1), .b(a1), .Cin(additionneur_1bit_1_cout), .S(S1), .Cout(additionneur_1bit_2_cout));
  additionneur_1bit additionneur_1bit_3 (
    .a(b2), .b(a2), .Cin(additionneur_1bit_2_cout), .S(S2), .Cout(additionneur_1bit_3_cout));
  additionneur_1bit additionneur_1bit_4 (.a(b3), .b(a3), .Cin(additionneur_1bit_3_cout), .S(S3));  // open: Cout
endmodule
