// Digital circuit b_type.dig as structural Verilog
module b_type (
  input  [31:0] rs1_rs2,
  input  [2:0] fct3,
  output Pris_nonPris
);

  wire not_1_out, not_2_out, or_1_out;

  or or_1 (or_1_out, rs1_rs2[0], rs1_rs2[1], rs1_rs2[2], rs1_rs2[3], rs1_rs2[4], rs1_rs2[5], rs1_rs2[6], rs1_rs2[7], rs1_rs2[8], rs1_rs2[9], rs1_rs2[10], rs1_rs2[11], rs1_rs2[12], rs1_rs2[13], rs1_rs2[14], rs1_rs2[15], rs1_rs2[16], rs1_rs2[17], rs1_rs2[18], rs1_rs2[19], rs1_rs2[20], rs1_rs2[21], rs1_rs2[22], rs1_rs2[23], rs1_rs2[24], rs1_rs2[25], rs1_rs2[26], rs1_rs2[27], rs1_rs2[28], rs1_rs2[29], rs1_rs2[30], rs1_rs2[31]);
  not not_1 (not_1_out, or_1_out);
  not not_2 (not_2_out, rs1_rs2[31]);
  Multiplexer #(.Selector_Bits(2)) multiplexer_1 (
    .sel({fct3[2], fct3[0]}), .in_0(not_1_out), .in_1(or_1_out), .in_2(rs1_rs2[31]), .in_3(not_2_out),
    .out(Pris_nonPris));
endmodule
