// Digital circuit breg32.dig as structural Verilog
module breg32 (
  input  [4:0] RD,
  input  [4:0] RS1,
  input  [4:0] RS2,
  input  [31:0] RES,
  input  WREG,
  output [31:0] src1,
  output [31:0] src2
);

  wire and_1_out, and_2_out, and_3_out, and_4_out, decoder_1_out_0, decoder_1_out_1, decoder_1_out_2,
       decoder_1_out_3, decoder_2_out_0, decoder_2_out_1, decoder_2_out_2, decoder_2_out_3, decoder_3_out_0,
       decoder_3_out_1, decoder_3_out_2, decoder_3_out_3;
  wire [31:0] breg8_0_1_src1, breg8_0_1_src2, breg8_1_src1, breg8_1_src2, breg8_2_src1, breg8_2_src2,
       breg8_3_src1, breg8_3_src2;

  Decoder #(.Selector_Bits(2)) decoder_1 (
    .sel(RD[4:3]), .out_0(decoder_1_out_0), .out_1(decoder_1_out_1), .out_2(decoder_1_out_2),
    .out_3(decoder_1_out_3));
  and and_1 (and_1_out, decoder_1_out_0, WREG);
  and and_2 (and_2_out, decoder_1_out_1, WREG);
  and and_3 (and_3_out, decoder_1_out_2, WREG);
  and and_4 (and_4_out, decoder_1_out_3, WREG);
  breg8_0 breg8_0_1 (
    .Reg(RD[2:0]), .res(RES), .Wreg(and_1_out), .rs1(RS1[2:0]), .rs2(RS2[2:0]), .src1(breg8_0_1_src1),
    .src2(breg8_0_1_src2));
  breg8 breg8_1 (
    .Reg(RD[2:0]), .res(RES), .Wreg(and_2_out), .rs1(RS1[2:0]), .rs2(RS2[2:0]), .src1(breg8_1_src1),
    .src2(breg8_1_src2));
  breg8 breg8_2 (
    .Reg(RD[2:0]), .res(RES), .Wreg(and_3_out), .rs1(RS1[2:0]), .rs2(RS2[2:0]), .src1(breg8_2_src1),
    .src2(breg8_2_src2));
  breg8 breg8_3 (
    .Reg(RD[2:0]), .res(RES), .Wreg(and_4_out), .rs1(RS1[2:0]), .rs2(RS2[2:0]), .src1(breg8_3_src1),
    .src2(breg8_3_src2));
  assign src1 = decoder_2_out_0 ? breg8_0_1_src1 : 32'bz;  // Driver driver_1
  assign src1 = decoder_2_out_1 ? breg8_1_src1 : 32'bz;  // Driver driver_2
  Decoder #(.Selector_Bits(2)) decoder_2 (
    .sel(RS1[4:3]), .out_0(decoder_2_out_0), .out_1(decoder_2_out_1), .out_2(decoder_2_out_2),
    .out_3(decoder_2_out_3));
  assign src1 = decoder_2_out_2 ? breg8_2_src1 : 32'bz;  // Driver driver_3
  assign src1 = decoder_2_out_3 ? breg8_3_src1 : 32'bz;  // Driver driver_4
  assign src2 = decoder_3_out_0 ? breg8_0_1_src2 : 32'bz;  // Driver driver_5
  assign src2 = decoder_3_out_1 ? breg8_1_src2 : 32'bz;  // Driver driver_6
  Decoder #(.Selector_Bits(2)) decoder_3 (
    .sel(RS2[4:3]), .out_0(decoder_3_out_0), .out_1(decoder_3_out_1), .out_2(decoder_3_out_2),
    .out_3(decoder_3_out_3));
  assign src2 = decoder_3_out_2 ? breg8_2_src2 : 32'bz;  // Driver driver_7
  assign src2 = decoder_3_out_3 ? breg8_3_src2 : 32'bz;  // Driver driver_8
endmodule
