// Digital circuit circuit_and.dig as structural Verilog
module circuit_and (
  input  b0,
  input  a0,
  input  b1,
  input  a1,
  input  b2,
  input  a2,
  input  b3,
  input  a3,
  output s0,
  output s1,
  output s2,
  output s3
);

  and and_1 (s3, a3, b3);
  and and_2 (s2, a2, b2);
  and and_3 (s1, a1, b1);
  and and_4 (s0, a0, b0);
endmodule
