// Digital circuit decaleur_4bit.dig as structural Verilog
module decaleur_4bit (
  input  e0,
  input  e1,
  input  e2,
  input  e3,
  input  [1:0] c,
  output s0,
  output s1,
  output s2,
  output s3
);

  Multiplexer #(.Selector_Bits(2)) multiplexer_1 (.sel(c), .in_0(e0), .in_1(e1), .in_2(e2), .in_3(e3), .out(s0));
  Multiplexer #(.Selector_Bits(2)) multiplexer_2 (.sel(c), .in_0(e1), .in_1(e2), .in_2(e3), .in_3(1'b0), .out(s1));
  Multiplexer #(.Selector_Bits(2)) multiplexer_3 (.sel(c), .in_0(e2), .in_1(e3), .in_2(1'b0), .in_3(1'b0), .out(s2));
  Multiplexer #(.Selector_Bits(2)) multiplexer_4 (.sel(c), .in_0(e3), .in_1(1'b0), .in_2(1'b0), .in_3(1'b0), .out(s3));
endmodule
