// Digital circuit processeur.dig as structural Verilog
module processeur (
  input  GATE_RES,
  input  W_MAR,
  input  W_PC,
  input  GATE_PC,
  input  OE,
  input  WE,
  input  MUX_MDR,
  input  GATE_MDR,
  input  W_REG,
  input  W_MDR,
  input  W_RI,
  input  MUX_JALR,
  input  MUX_UAL,
  input  GATE_SRC2,
  input  MUX_SW,
  input  FCT7,
  output [6:0] OPcode,
  output cout,
  output cout_2
);

  wire b_type_1_pris_nonpris, multiplexer_6_out, not_1_out, not_2_out;
  wire [0:0] and_1_out;
  wire [11:0] multiplexer_3_out;
  wire [31:0] add_1_s, bitextender_1_out, bitextender_2_out, bitextender_3_out, breg32_1_src1, breg32_1_src2,
       driver_1_out, driver_2_out, driver_3_out, MAR_q, MDR_q, multiplexer_1_out, multiplexer_2_out,
       multiplexer_4_out, multiplexer_5_out, PC_q, ual_1_res;
  wire [31:7] RI_q;

  BitExtender #(.inputBits(21), .outputBits(32)) bitextender_1 (
    .in({RI_q[31], RI_q[19:12], RI_q[20], RI_q[30:21], 1'b0}), .out(bitextender_1_out));
  BitExtender #(.inputBits(13), .outputBits(32)) bitextender_2 (
    .in({RI_q[31], RI_q[7], RI_q[30:25], RI_q[11:8], 1'b0}), .out(bitextender_2_out));
  Multiplexer #(.Selector_Bits(2), .Bits(32)) multiplexer_1 (
    .sel({OPcode[2], and_1_out[0]}), .in_0(32'h4), .in_1(bitextender_2_out), .in_2(bitextender_1_out),
    .in_3({32{1'b0}}), .out(multiplexer_1_out));
  Add #(.Bits(32)) add_1 (.a(PC_q), .b(multiplexer_1_out), .c_i(1'b0), .s(add_1_s), .c_o(cout_2));
  Multiplexer #(.Bits(32)) multiplexer_2 (.sel(MUX_JALR), .in_0(add_1_s), .in_1(driver_1_out), .out(multiplexer_2_out));
  D_FF #(.Bits(32)) PC (.D(multiplexer_2_out), .C(W_PC), .Q(PC_q));  // open: nQ
  and and_1 (and_1_out[0], not_1_out, b_type_1_pris_nonpris);
  not not_1 (not_1_out, OPcode[2]);
  assign driver_1_out = GATE_PC ? PC_q : 32'bz;  // Driver driver_1
  D_FF #(.Bits(32)) RI (.D(driver_1_out), .C(W_RI), .Q({RI_q, OPcode}));  // open: nQ
  b_type b_type_1 (.rs1_rs2(driver_2_out), .fct3(RI_q[14:12]), .Pris_nonPris(b_type_1_pris_nonpris));
  D_FF #(.Bits(32)) MAR (.D(driver_1_out), .C(W_MAR), .Q(MAR_q));  // open: nQ
  assign driver_2_out = OPcode[6] ? ual_1_res : 32'bz;  // Driver driver_2
  Multiplexer #(.Bits(12)) multiplexer_3 (
    .sel(MUX_SW), .in_0(RI_q[31:20]), .in_1({RI_q[31:25], RI_q[11:7]}), .out(multiplexer_3_out));
  Multiplexer #(.Bits(32)) multiplexer_4 (
    .sel(MUX_MDR), .in_0(driver_1_out), .in_1(driver_3_out), .out(multiplexer_4_out));
  breg32 breg32_1 (
    .RD(RI_q[11:7]), .RS1(RI_q[19:15]), .RS2(RI_q[24:20]), .RES(driver_1_out), .WREG(W_REG),
    .src1(breg32_1_src1), .src2(breg32_1_src2));
  BitExtender #(.inputBits(12), .outputBits(32)) bitextender_3 (.in(multiplexer_3_out), .out(bitextender_3_out));
  assign driver_3_out = not_2_out ? MDR_q : 32'bz;  // Driver driver_3
  not not_2 (not_2_out, OE);
  assign driver_1_out = GATE_SRC2 ? breg32_1_src2 : 32'bz;  // Driver driver_4
  Multiplexer #(.Bits(32)) multiplexer_5 (
    .sel(MUX_UAL), .in_0(breg32_1_src2), .in_1(bitextender_3_out), .out(multiplexer_5_out));
  Multiplexer multiplexer_6 (.sel(FCT7), .in_0(RI_q[30]), .in_1(1'b1), .out(multiplexer_6_out));
  D_FF #(.Bits(32)) MDR (.D(multiplexer_4_out), .C(W_MDR), .Q(MDR_q));  // open: nQ
  assign driver_1_out = GATE_MDR ? MDR_q : 32'bz;  // Driver driver_5
  ual ual_1 (
    .src1(breg32_1_src1), .src2(multiplexer_5_out), .sub(multiplexer_6_out), .fct3(RI_q[14:12]),
    .res(ual_1_res), .cout(cout));
  RAMSinglePortSel #(.AddrBits(8), .Bits(32)) ramsingleportsel_1 (
    .A(MAR_q[9:2]), .CS(1'b1), .WE(WE), .OE(OE), .D(driver_3_out));
  assign driver_1_out = GATE_RES ? ual_1_res : 32'bz;  // Driver driver_6
endmodule
